# Fritzing sketch PlatineAnschlagchip (saved by Fritzing 0.9.3b)
circuit board: 8.46667cm x 5.64444cm
breadboards: 1

parts:
  MH-ET_LIVE_ESP32_DEVKIT1 = MH-ET LIVE ESP32 DEVKIT 38 pins
  J1 = Camdenboss CTB0158-7 [part_number=CTB0158-7 package=THT]
  S1 = Toggle Switch [package=THT]
  S2 = Toggle Switch [package=THT]
  S3 = Toggle Switch [package=THT]
  S4 = Toggle Switch [package=THT]
  V1 = DC Power [voltage=3.3V]

nets:
  N1: MH-ET_LIVE_ESP32_DEVKIT1.3V3, J1.pin1, J1.pin2
  N2: MH-ET_LIVE_ESP32_DEVKIT1.IO34, J1.pin7
  N3: MH-ET_LIVE_ESP32_DEVKIT1.IO35, J1.pin6
  N4: MH-ET_LIVE_ESP32_DEVKIT1.IO32, J1.pin5
  N5: MH-ET_LIVE_ESP32_DEVKIT1.IO33, J1.pin4
  N6: MH-ET_LIVE_ESP32_DEVKIT1.GND#64, J1.pin3
  N7: J1.terminal_1, V1.V+
  N8: J1.terminal_2, S1.COM, S2.COM, S3.COM, S4.COM
  N9: J1.terminal_3, V1.V-
  N10: J1.terminal_4, S1.L1
  N11: J1.terminal_5, S2.L1
  N12: J1.terminal_6, S3.L1
  N13: J1.terminal_7, S4.L1

custom parts:
  MH-ET LIVE ESP32 DEVKIT 38 pins: http://mh.nodebb.com/topic/2/mh-et-live-esp32-devkit
